# Fritzing sketch squaresynth-step1 (saved by Fritzing 0.9.0b)
circuit board: 8.46667cm x 5.64444cm
breadboards: 1

parts:
  R4 = Resistor [tolerance=±5% resistance=1k package=THT]
  D1 = Rectifier Diode [part_number=1N4001 package="300 mil [THT]"]
  C1 = Electrolytic Capacitor [capacitance=22pF voltage=16V package="100 mil [THT, electrolytic]"]
  BAT1 = BC9VPC [package=bc9vpc]
  LED1 = LED - 5mm [color="White (4500K)" package="5 mm [THT]"]
  R7 = Resistor [tolerance=±5% resistance=1k package=THT]
  SP1 = SPEAKER [package=pcb_mount_speaker]
  BC2 = CD4093 [part_number=CD4093BC package="DIP14 [THT]"]
  Amp1 = Amplifier

nets:
  N1: R4.Pin_0, D1.anode, BC2.L
  N2: R4.Pin_1, C1.+, BC2.E
  N3: D1.cathode, Amp1.IN
  N4: C1.-, BAT1.V-, R7.Pin_1, BC2.GND, Amp1.GND#2, Amp1.GND#4
  VCC: BAT1.V+, LED1.anode, BC2.A, BC2.H, BC2.VCC, Amp1.VCC
  N5: LED1.cathode, R7.Pin_0
  N6: SP1.+, Amp1.OUT
  N7: SP1.-, Amp1.GND#6
  N8: BC2.J, BC2.C
  N9: BC2.F, BC2.M

custom parts:
  CD4093: Quad NAN Schmitt Trigger
  Amplifier: LM386 based Amplifier
