# Fritzing sketch squaresynth-step3 (saved by Fritzing 0.9.0b)
circuit board: 8.46667cm x 5.64444cm
breadboards: 1

parts:
  R4 = Resistor [tolerance=±5% resistance=1k package=THT]
  C3 = Ceramic Capacitor [capacitance=2.2µF package="100 mil [THT, multilayer]"]
  R5 = Rotary Potentiometer (Small) [maximum_resistance=200kΩ package=THT]
  D1 = Rectifier Diode [part_number=1N4001 package="300 mil [THT]"]
  C1 = Electrolytic Capacitor [capacitance=22pF voltage=16V package="100 mil [THT, electrolytic]"]
  BAT1 = BC9VPC [package=bc9vpc]
  LED1 = LED - 5mm [color="White (4500K)" package="5 mm [THT]"]
  R7 = Resistor [tolerance=±5% resistance=1k package=THT]
  SP1 = SPEAKER [package=pcb_mount_speaker]
  BC2 = CD4093 [part_number=CD4093BC package="DIP14 [THT]"]
  Amp1 = Amplifier
  D2 = Rectifier Diode [part_number=1N4001 package="300 mil [THT]"]
  C4 = Electrolytic Capacitor [capacitance=1µF package="100 mil [THT, electrolytic]"]
  R2 = Resistor [tolerance=±5% resistance=1k package=THT]

nets:
  N1: R4.Pin_0, D1.anode, BC2.L
  N2: R4.Pin_1, C1.+, BC2.E
  N3: C3.0, R5.leg1, BC2.G
  N4: C3.1, C1.-, BAT1.V-, R7.Pin_1, BC2.GND, Amp1.GND#2, Amp1.GND#4, C4.-
  N5: R5.wiper, BC2.F, BC2.M
  N6: D1.cathode, Amp1.IN, D2.cathode
  VCC: BAT1.V+, LED1.anode, BC2.A, BC2.H, BC2.VCC, Amp1.VCC
  N7: LED1.cathode, R7.Pin_0
  N8: SP1.+, Amp1.OUT
  N9: SP1.-, Amp1.GND#6
  N10: BC2.J, BC2.C
  N11: BC2.K, D2.anode, R2.Pin_0
  N12: BC2.D, C4.+, R2.Pin_1

custom parts:
  CD4093: Quad NAN Schmitt Trigger
  Amplifier: LM386 based Amplifier
