# Fritzing sketch squaresynth (saved by Fritzing 0.9.0b)
circuit board: 8.46667cm x 5.64444cm
breadboards: 1

parts:
  R2 = Resistor [tolerance=±5% resistance=1k package=THT]
  R4 = Resistor [tolerance=±5% resistance=1k package=THT]
  C2 = Tantalum Capacitor [capacitance=10pF package="100 mil [THT, tantalum]"]
  C3 = Ceramic Capacitor [capacitance=2.2µF package="100 mil [THT, multilayer]"]
  C4 = Electrolytic Capacitor [capacitance=1µF package="100 mil [THT, electrolytic]"]
  R5 = Rotary Potentiometer (Small) [maximum_resistance=200kΩ package=THT]
  D1 = Rectifier Diode [part_number=1N4001 package="300 mil [THT]"]
  D2 = Rectifier Diode [part_number=1N4001 package="300 mil [THT]"]
  C1 = Electrolytic Capacitor [capacitance=22pF package="100 mil [THT, electrolytic]"]
  R6 = Photocell (LDR) [package=THT]
  BAT1 = BC9VPC [package=bc9vpc]
  BC1 = CD4093 [part_number=CD4093BC package="DIP14 [THT]"]
  SPKR1 = Loudspeaker
  LED1 = LED - 5mm [color="White (4500K)" package="5 mm [THT]"]
  R7 = Resistor [tolerance=±5% resistance=1k package=THT]

nets (from the schematic view):
  N1: R2.Pin_0, D2.anode, BC1.K
  N2: R2.Pin_1, C4.+, BC1.D
  N3: R4.Pin_0, D1.anode, BC1.L
  N4: R4.Pin_1, C1.+, BC1.E
  N5: C2.-, C3.1, C4.-, C1.-, BAT1.V-, BC1.GND, R7.Pin_1
  N6: C2.+, R6.pin_1, BC1.B
  N7: C3.0, R5.leg1, BC1.G
  N8: R5.wiper, BC1.F, BC1.M
  N9: D1.cathode, D2.cathode, SPKR1.pin1
  N10: R6.pin_0, BC1.J, BC1.C
  N11: BAT1.V+, BC1.VCC, LED1.anode
  N12: BC1.A, BC1.H
  N13: LED1.cathode, R7.Pin_0

custom parts:
  CD4093: Quad NAN Schmitt Trigger
